# Fritzing sketch default_sketch (saved by Fritzing 0.9.3b)

parts:
  OLED1 = OLED 128x64 I2C Monochrome Display VDD-GND
  A1 = XIAO ESP32C3-tht
  S2 = Momentary Switch [package=ksa_sealed_tac_switch]
  JP1 = Header 3 [package=screwterminal-3.5mm-3_lock.007s]

nets:
  N1: OLED1.VDD, A1.Pin_22
  N2: OLED1.GND, A1.Pin_2, A1.Pin_21, S2.1, JP1.1
  N3: OLED1.SCK, A1.Pin_14, JP1.3
  N4: OLED1.SDA, A1.Pin_13, JP1.2
  N5: A1.Pin_17, S2.3

notes:
  To VGA Ground
  To VGA DDC Data
  To VGA DDC Clock

custom parts:
  OLED 128x64 I2C Monochrome Display VDD-GND: OLED 128x64 I2C Monochrome Display. Note: there are two variants of this part, this one is the VDD GND SCK SDA variant. The other is GND VDD SCK SDA. Make sure you select the part that matches your module as using the incorrect part will probably destroy your module! In addition the mounting holes are marked on silkscreen but not by default drilled. If you want drilled mounting holes, copy a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
  XIAO ESP32C3-tht: Seeed Studio XIAO ESP32C3 adopts new RISC-V architecture, supporting both Wi-Fi and BLE wireless connectivities.
